// Logisim project branch_comp.circ as structural Verilog: 1 circuit, main circuit branch_comp
module branch_comp (
  input  [31:0] rs1,
  input  [31:0] rs2,
  input  BrUn,
  output BrEq,
  output BrLt
);

  wire comparator_1_lt, multiplexer_1_out, not_1_out, xor_1_out;

  Comparator #(.width(32)) comparator_1 (.a(rs1), .b(rs2), .eq(BrEq), .lt(comparator_1_lt));  // open: gt
  // XOR_Gate xor_1 has open pins: out=xor_1_out
  Multiplexer #(.enable("false")) multiplexer_1 (
    .in0(comparator_1_lt), .in1(not_1_out), .out(multiplexer_1_out), .sel(xor_1_out));
  not not_1 (not_1_out, comparator_1_lt);
  Multiplexer #(.enable("false")) multiplexer_2 (
    .in0(comparator_1_lt), .in1(multiplexer_1_out), .out(BrLt), .sel(BrUn));

  // Notes on the sheet:
  //   INPUTS to your circuit
  //   DON'T CHANGE THE LOCATIONS OF THE INPUTS AND OUTPUTS!
  //   OUTPUT from your circuit
endmodule
