// Logisim project control_logic.circ as structural Verilog: 1 circuit, main circuit control_logic
module control_logic (
  input  [31:0] inst,
  input  BrEq,
  input  BrLt,
  output PCSel,
  output RegWEn,
  output [2:0] ImmSel,
  output BrUn,
  output ASel,
  output BSel,
  output [3:0] ALUSel,
  output MemRW,
  output [1:0] WBSel,
  output CSRSel,
  output CSRWen
);

  wire [6:5] a_alu, a_pc;
  wire [31:0] rom_2_data, rom_3_data;
  wire [31:16] cw;

  ROM #(.dataWidth(32)) rom_1 (
    .addr({inst[14:12], inst[6:2]}),
    .data({cw, BrUn, a_pc, a_alu, CSRWen, CSRSel, WBSel, MemRW, ASel, BSel, ImmSel, RegWEn}));
  ROM #(.dataWidth(32)) rom_2 (.addr({1'b0, a_alu, inst[25], inst[30], inst[14:12]}), .data(rom_2_data));
  ROM #(.dataWidth(32)) rom_3 (.addr({1'b0, a_pc, BrLt, BrEq, inst[14:12]}), .data(rom_3_data));
  Bit_Extender #(.in_width(32), .out_width(4), .\type ("zero")) bit_extender_1 (.in(rom_2_data), .out(ALUSel));
  Bit_Extender #(.in_width(32), .out_width(1), .\type ("zero")) bit_extender_2 (.in(rom_3_data), .out(PCSel));

  // Other names for the same wires on the sheet: a_alu[4:0] = {inst[25], inst[30], inst[14:12]}; i30 = inst[30];
  //   i25 = inst[25]; a_main[7:0] = {inst[14:12], inst[6:2]}; op5[4:0] = inst[6:2];
  //   a_pc[4:0] = {BrLt, BrEq, inst[14:12]}; f3[2:0] = inst[14:12];
  //   cw[15:0] = {BrUn, a_pc, a_alu, CSRWen, CSRSel, WBSel, MemRW, ASel, BSel, ImmSel, RegWEn}; aluMode[1:0] = a_alu;
  //   isBr = a_pc[5]; isJ = a_pc[6]

  // Notes on the sheet:
  //   INPUTS to your circuit
  //   Fields: op5 = inst[6:2], f3 = funct3, i30 = inst[30], i25 = inst[25]
  //   contents of rom_1 (hex, n*v repeats v):
  //   11 0 0 0 1891 b7 0 0 52 0 0 0 1081 897 10*0 2034 4111 0 4139 4*0 11 0 0 0 1891 b7 0 0 52 0 0 0 1081
  //   897 10*0 2034 0 0 4139 400 0 0 0 11 0 0 0 1891 b7 0 0 52 0 0 0 1081 897 13*0 4139 9*0 b7 6*0 1081
  //   897 13*0 4139 8*0 1891 b7 6*0 1081 897 10*0 2034 0 0 4139 8*0 1891 b7 6*0 1081 897 10*0 2034 0 0
  //   4139 600 7*0 1891 b7 6*0 1081 897 10*0 a034 0 0 4139 8*0 1891 b7 6*0 1081 897 10*0 a034 0 0 4139
  //   contents of rom_2 (hex, n*v repeats v):
  //   32*0 32*d 0 6 7 0 3 4 2 1 c 6 7 0 3 5 2 1 a e 0 b 4*0 a e 0 b 5*0 6 7 0 3 4 2 1 0 6 7 0 3 5 2 1 0 6
  //   7 0 3 4 2 1 0 6 7 0 3 5 2 1 32*0 32*d 0 6 7 0 3 4 2 1 c 6 7 0 3 5 2 1 a e 0 b 4*0 a e 0 b 5*0 6 7 0
  //   3 4 2 1 0 6 7 0 3 5 2 1 0 6 7 0 3 4 2 1 0 6 7 0 3 5 2 1
  //   contents of rom_3 (hex, n*v repeats v):
  //   33*0 1 0 0 0 1 0 1 1 4*0 1 0 1 0 1 0 0 1 0 1 0 1 0 0 0 1 0 1 0 64*1 33*0 1 0 0 0 1 0 1 1 4*0 1 0 1 0
  //   1 0 0 1 0 1 0 1 0 0 0 1 0 1 0 64*1
  //   DON'T CHANGE THE LOCATIONS OF THE INPUTS AND OUTPUTS!
  //   OUTPUT from your circuit
  //   Main decoder ROM: addr {funct3, opcode[6:2]} -> control word
  //   ALUSel ROM: addr {aluMode, inst[25], inst[30], funct3}; aluMode 0=add 1=bsel 2=R 3=I
  //   PCSel ROM: addr {isJump, isBranch, BrLt, BrEq, funct3}  (kill = PCSel)
endmodule
