// Logisim project cpu.circ as structural Verilog: 1 circuit, main circuit cpu
module cpu (
  input  clk,
  input  [31:0] INSTRUCTION,
  input  [31:0] READ_DATA,
  output [31:0] WRITE_ADDRESS,
  output [31:0] PROGRAM_COUNTER,
  output [31:0] ra,
  output [31:0] sp,
  output [31:0] t0,
  output [31:0] t1,
  output [31:0] t2,
  output [31:0] s0,
  output [31:0] s1,
  output [31:0] a0,
  output [31:0] tohost,
  output [3:0] WRITE_ENABLE,
  output [31:0] WRITE_DATA
);

  wire ASel, BrEq, BrLt, BrUn, BSel, comparator_1_eq, CSRSel, CSRWen, func3_bit0, MemRW, PCSel, RegWEn,
       sh_mask_bit1;
  wire [1:0] WBSel;
  wire [2:0] ImmSel;
  wire [3:0] ALUSel, bit_extender_2_out, shifter_1_out;
  wire [7:0] shifter_3_out, shifter_3_out_2, shifter_3_out_3, shifter_3_out_4;
  wire [11:0] CSR_ADDRESS;
  wire [19:0] EX_INSTRUCTION;
  wire [31:0] adder_1_out, bit_extender_1_out, bit_extender_4_out, bit_extender_5_out, EX_PROGRAM_COUNTER,
       imm, multiplexer_1_out, multiplexer_2_out, multiplexer_3_out, multiplexer_4_out, multiplexer_5_out,
       multiplexer_7_out, multiplexer_8_out, rs1, rs2;

  Adder #(.width(32)) adder_1 (.a(PROGRAM_COUNTER), .b(32'h4), .out(adder_1_out));  // open: cin, cout
  Multiplexer #(.enable("false"), .width(32)) multiplexer_1 (
    .in0(adder_1_out), .in1({WRITE_ADDRESS[31:1], 1'b0}), .out(multiplexer_1_out), .sel(PCSel));
  Register #(.width(32)) PC (.D(multiplexer_1_out), .clk(clk), .Q(PROGRAM_COUNTER));  // open: en, clr
  imm_gen imm_gen_1 (.inst({CSR_ADDRESS, EX_INSTRUCTION}), .ImmSel(ImmSel), .imm(imm));
  Multiplexer #(.enable("false"), .width(32)) multiplexer_2 (
    .in0(INSTRUCTION), .in1(32'h13), .out(multiplexer_2_out), .sel(PCSel));
  Register #(.width(64)) register_1 (
    .D({PROGRAM_COUNTER, multiplexer_2_out}), .clk(clk), .Q({EX_PROGRAM_COUNTER, CSR_ADDRESS, EX_INSTRUCTION}));  // open: en, clr
  Multiplexer #(.enable("false"), .width(32)) multiplexer_3 (
    .in0(rs1), .in1(EX_PROGRAM_COUNTER), .out(multiplexer_3_out), .sel(ASel));
  Multiplexer #(.enable("false"), .width(32)) multiplexer_4 (.in0(rs2), .in1(imm), .out(multiplexer_4_out), .sel(BSel));
  branch_comp branch_comp_1 (.rs1(rs1), .rs2(rs2), .BrUn(BrUn), .BrEq(BrEq), .BrLt(BrLt));
  alu alu_1 (.Result(WRITE_ADDRESS), .A(multiplexer_3_out), .B(multiplexer_4_out), .ALUSel(ALUSel));
  assign bit_extender_1_out = {{27{1'b0}}, EX_INSTRUCTION[19:15]};  // Bit_Extender bit_extender_1
  Multiplexer #(.enable("false"), .width(32)) multiplexer_5 (
    .in0(rs1), .in1(bit_extender_1_out), .out(multiplexer_5_out), .sel(CSRSel));
  control_logic control_logic_1 (
    .CSRWen(CSRWen), .PCSel(PCSel), .RegWEn(RegWEn), .ImmSel(ImmSel), .BrUn(BrUn), .ASel(ASel), .BSel(BSel),
    .ALUSel(ALUSel), .MemRW(MemRW), .WBSel(WBSel), .CSRSel(CSRSel), .inst({CSR_ADDRESS, EX_INSTRUCTION}),
    .BrEq(BrEq), .BrLt(BrLt));
  Shifter #(.width(4)) shifter_1 (.in({2'b00, sh_mask_bit1, MemRW}), .\dist (WRITE_ADDRESS[1:0]), .out(shifter_1_out));
  assign bit_extender_2_out = {{3{MemRW}}, MemRW};  // Bit_Extender bit_extender_2
  Shifter #(.width(32)) shifter_2 (.in(rs2), .\dist ({WRITE_ADDRESS[1:0], 3'b000}), .out(WRITE_DATA));
  csr csr_1 (.CSR_address(CSR_ADDRESS), .CSR_din(multiplexer_5_out), .CSR_WE(CSRWen), .clk(clk), .tohost(tohost));
  Bit_Extender #(.in_width(3), .out_width(1)) bit_extender_3 (.in(EX_INSTRUCTION[14:12]), .out(func3_bit0));
  Shifter #(.shift("ar"), .width(32)) shifter_3 (
    .in(READ_DATA), .\dist ({WRITE_ADDRESS[1:0], 3'b000}),
    .out({shifter_3_out_4, shifter_3_out_3, shifter_3_out_2, shifter_3_out}));
  Multiplexer #(.enable("false"), .width(4)) multiplexer_6 (
    .in0(shifter_1_out), .in1(bit_extender_2_out), .out(WRITE_ENABLE), .sel(comparator_1_eq));
  Comparator #(.width(3)) comparator_1 (.a(EX_INSTRUCTION[14:12]), .b(3'b010), .eq(comparator_1_eq));  // open: gt, lt
  and and_1 (sh_mask_bit1, MemRW, func3_bit0);
  assign bit_extender_4_out = {{24{shifter_3_out[7]}}, shifter_3_out};  // Bit_Extender bit_extender_4
  assign bit_extender_5_out = {{16{shifter_3_out_2[7]}}, {shifter_3_out_2, shifter_3_out}};  // Bit_Extender bit_extender_5
  Multiplexer #(.enable("false"), .select(3), .width(32)) multiplexer_7 (
    .in0(bit_extender_4_out), .in1(bit_extender_5_out),
    .in2({shifter_3_out_4, shifter_3_out_3, shifter_3_out_2, shifter_3_out}), .out(multiplexer_7_out),
    .sel(EX_INSTRUCTION[14:12]));  // open: in3, in4, in5, in6, in7
  Multiplexer #(.enable("false"), .select(2), .width(32)) multiplexer_8 (
    .in0(multiplexer_7_out), .in1(WRITE_ADDRESS), .in2(PROGRAM_COUNTER), .out(multiplexer_8_out), .sel(WBSel));  // open: in3
  regfile regfile_1 (
    .rs1(EX_INSTRUCTION[19:15]), .rs2(CSR_ADDRESS[4:0]), .rd(EX_INSTRUCTION[11:7]),
    .Write_Data(multiplexer_8_out), .RegWEn(RegWEn), .clk(clk), .ra(ra), .sp(sp), .t0(t0), .t1(t1), .t2(t2),
    .s0(s0), .s1(s1), .a0(a0), .Read_Data_1(rs1), .Read_Data_2(rs2));

  // Other names for the same wires on the sheet: ALU_RESULT[31:0] = WRITE_ADDRESS;
  //   rd_index[4:0] = EX_INSTRUCTION[11:7]; func3[2:0] = EX_INSTRUCTION[14:12];
  //   rs1_index[4:0] = EX_INSTRUCTION[19:15]; EX_INSTRUCTION[31:20] = CSR_ADDRESS; rs2_index[4:0] = CSR_ADDRESS[4:0]

  // Notes on the sheet:
  //   Output to IMEM
  //   IMEM (do **NOT** move this)
  //   Inputs from IMEM
  //   It is OK to move the PC, RegFile, ALU, MEM, Branch Comp, Imm Gen, and Control Logic to wherever is most convenient for you when constructing your CPU, and to delete this text
  //   Inputs/Outputs for testing. Do **NOT** move these.
  //   sh base mask bit1 = MemRW & funct3[0]  (sb: 0001, sh: 0011)
  //   Outputs To DMEM
  //   DMEM (do **NOT** move this)
  //   Inputs From DMEM
endmodule
